// Logisim project circuitoEntradas_Final.circ as structural Verilog: 4 circuits, main circuit main
module main (
  input  A,
  input  B,
  input  C,
  input  D,
  input  E,
  output L0,
  output L1,
  output L2,
  output L3,
  output L4,
  output L5
);

  wire nand_1_out, nand_2_out, nand_3_out, nand_4_out, nand_5_out, nand_6_out, nand_7_out, nand_8_out,
       nand_9_out, nand_10_out, nand_11_out, nand_12_out, nand_13_out, nand_14_out, nand_15_out, nand_16_out,
       nand_17_out, nand_18_out, nand_19_out, nand_20_out, nand_21_out, nand_22_out, nand_23_out,
       nand_24_out, nand_25_out, nand_26_out, nand_27_out, nand_28_out, nand_29_out, nand_30_out,
       nand_31_out, nand_32_out, nand_33_out, nand_34_out, nand_35_out, nand_36_out, nand_37_out,
       nand_38_out, nand_39_out, nand_40_out, nand_41_out, nand_42_out, nand_43_out, nand_44_out,
       nand_45_out, nand_46_out, nand_47_out, nand_48_out, nand_49_out, nand_50_out, nand_51_out,
       nand_52_out, nand_53_out, nand_54_out, nand_55_out, nand_56_out, nand_57_out, nand_58_out,
       nand_59_out, nand_60_out, nand_61_out, nand_62_out, nand_63_out, nand_64_out, nand_65_out,
       nand_66_out, nand_67_out, nand_68_out, nand_69_out, nand_70_out, nand_71_out, nand_72_out,
       nand_73_out, nand_74_out, nand_75_out, nand_76_out, nand_77_out, nand_78_out, nand_79_out,
       nand_80_out, nand_81_out, nand_82_out, nand_83_out, nand_84_out, nand_85_out, nand_86_out,
       nand_87_out, nand_88_out, nand_89_out, nand_90_out, nand_91_out, nand_92_out, nand_93_out,
       nand_94_out, nand_95_out, nand_96_out, nand_97_out, nand_98_out, nand_99_out, nand_100_out,
       nand_101_out, nand_102_out, nand_103_out, nand_104_out, nand_105_out, nand_106_out, nand_107_out,
       nand_108_out, nand_109_out, nand_110_out, nand_111_out, nand_112_out, nand_113_out, nand_114_out,
       nand_115_out, nand_116_out, nand_117_out, nand_118_out, nand_119_out, nand_120_out, nand_121_out,
       nand_122_out, nand_123_out, nand_124_out, nand_125_out, nand_126_out, nand_127_out, nand_128_out,
       nand_129_out, nand_130_out, nand_131_out, nand_132_out, nand_133_out, nand_134_out, nand_135_out,
       nand_136_out, nand_137_out, nand_138_out, nand_139_out, nand_140_out, nand_141_out, nand_142_out,
       nand_143_out, nand_144_out, nand_145_out, nand_146_out, nand_147_out, nand_148_out, nand_149_out,
       nand_150_out, nand_151_out, nand_152_out, nand_153_out, nand_154_out, nand_155_out, nand_156_out,
       nand_157_out, nand_158_out, nand_159_out, nand_160_out, nand_161_out, nand_162_out, nand_163_out,
       nand_164_out, nand_165_out, nand_166_out, nand_167_out, nand_168_out, nand_169_out, nand_170_out,
       nand_171_out, nand_172_out, nand_173_out, nand_174_out, nand_175_out, nand_176_out, nand_177_out,
       nand_178_out, nand_179_out, nand_180_out, nand_181_out, nand_182_out, nand_183_out, nand_184_out,
       nand_185_out, nand_186_out, nand_187_out, nand_188_out, nand_189_out, nand_190_out, nand_191_out,
       nand_192_out, nand_193_out, nand_194_out, nand_195_out, nand_196_out, nand_197_out, nand_198_out,
       nand_199_out, nand_200_out, nand_201_out, nand_202_out, nand_203_out, nand_204_out, nand_205_out,
       nand_206_out, nand_207_out, nand_208_out, nand_209_out, nand_210_out, nand_211_out, nand_212_out,
       nand_213_out, nand_214_out, nand_215_out, nand_216_out, nand_217_out, nand_218_out, nand_219_out,
       nand_220_out, nand_221_out, nand_222_out, nand_223_out, nand_224_out, nand_225_out, nand_226_out,
       nand_227_out, nand_228_out, nand_229_out, nand_230_out, nand_231_out, nand_232_out, nand_233_out,
       nand_234_out, nand_235_out, nand_236_out, nand_237_out, nand_238_out, nand_239_out, nand_240_out,
       nand_241_out, nand_242_out, nand_243_out, nand_244_out, nand_245_out, nand_246_out, nand_247_out,
       nand_248_out, nand_249_out, nand_250_out, nand_251_out, nand_252_out, nand_253_out, nand_254_out,
       nand_255_out, nand_256_out, nand_257_out, nand_258_out, nand_259_out, nand_260_out, nand_261_out,
       nand_262_out, nand_264_out, nand_265_out, nand_266_out, nand_267_out, nand_268_out, nand_269_out,
       nand_270_out, nand_271_out, nand_272_out, nand_273_out;

  nand nand_1 (nand_1_out, B, B);
  nand nand_2 (nand_2_out, D, D);
  nand nand_3 (nand_3_out, B, B);
  nand nand_4 (nand_4_out, A, A);
  nand nand_5 (nand_5_out, A, A);
  nand nand_6 (nand_6_out, D, D);
  nand nand_7 (nand_7_out, E, E);
  nand nand_8 (nand_8_out, C, C);
  nand nand_9 (nand_9_out, A, A);
  nand nand_10 (nand_10_out, C, C);
  nand nand_11 (nand_11_out, E, E);
  nand nand_12 (nand_12_out, B, B);
  nand nand_13 (nand_13_out, A, A);
  nand nand_14 (nand_14_out, D, D);
  nand nand_15 (nand_15_out, E, E);
  nand nand_16 (nand_16_out, B, B);
  nand nand_17 (nand_17_out, A, A);
  nand nand_18 (nand_18_out, A, A);
  nand nand_19 (nand_19_out, B, B);
  nand nand_20 (nand_20_out, B, B);
  nand nand_21 (nand_21_out, B, B);
  nand nand_22 (nand_22_out, C, C);
  nand nand_23 (nand_23_out, B, B);
  nand nand_24 (nand_24_out, A, A);
  nand nand_25 (nand_25_out, B, B);
  nand nand_26 (nand_26_out, E, E);
  nand nand_27 (nand_27_out, A, A);
  nand nand_28 (nand_28_out, D, D);
  nand nand_29 (nand_29_out, A, A);
  nand nand_30 (nand_30_out, E, E);
  nand nand_31 (nand_31_out, A, A);
  nand nand_32 (nand_32_out, B, B);
  nand nand_33 (nand_33_out, D, D);
  nand nand_34 (nand_34_out, B, B);
  nand nand_35 (nand_35_out, D, D);
  nand nand_36 (nand_36_out, E, E);
  nand nand_37 (nand_37_out, B, B);
  nand nand_38 (nand_38_out, A, A);
  nand nand_39 (nand_39_out, C, C);
  nand nand_40 (nand_40_out, E, E);
  nand nand_41 (nand_41_out, A, A);
  nand nand_42 (nand_42_out, C, C);
  nand nand_43 (nand_43_out, D, D);
  nand nand_44 (nand_44_out, B, B);
  nand nand_45 (nand_45_out, B, B);
  nand nand_46 (nand_46_out, C, C);
  nand nand_47 (nand_47_out, D, D);
  nand nand_48 (nand_48_out, C, C);
  nand nand_49 (nand_49_out, E, E);
  nand nand_50 (nand_50_out, nand_1_out, nand_2_out);
  nand nand_51 (nand_51_out, nand_3_out, D);
  nand nand_52 (nand_52_out, nand_4_out, D);
  nand nand_53 (nand_53_out, nand_5_out, B);
  nand nand_54 (nand_54_out, nand_6_out, nand_7_out);
  nand nand_55 (nand_55_out, A, nand_8_out);
  nand nand_56 (nand_56_out, nand_9_out, nand_10_out);
  nand nand_57 (nand_57_out, D, nand_11_out);
  nand nand_58 (nand_58_out, nand_12_out, C);
  nand nand_59 (nand_59_out, nand_13_out, B);
  nand nand_60 (nand_60_out, nand_14_out, nand_15_out);
  nand nand_61 (nand_61_out, A, nand_16_out);
  nand nand_62 (nand_62_out, nand_17_out, B);
  nand nand_63 (nand_63_out, D, E);
  nand nand_64 (nand_64_out, nand_18_out, B);
  nand nand_65 (nand_65_out, A, nand_19_out);
  nand nand_66 (nand_66_out, A, nand_20_out);
  nand nand_67 (nand_67_out, A, nand_21_out);
  nand nand_68 (nand_68_out, A, nand_22_out);
  nand nand_69 (nand_69_out, nand_23_out, D);
  nand nand_70 (nand_70_out, nand_24_out, nand_25_out);
  nand nand_71 (nand_71_out, C, nand_26_out);
  nand nand_72 (nand_72_out, nand_27_out, B);
  nand nand_73 (nand_73_out, nand_28_out, E);
  nand nand_74 (nand_74_out, nand_29_out, B);
  nand nand_75 (nand_75_out, D, nand_30_out);
  nand nand_76 (nand_76_out, nand_31_out, nand_32_out);
  nand nand_77 (nand_77_out, C, nand_33_out);
  nand nand_78 (nand_78_out, nand_34_out, C);
  nand nand_79 (nand_79_out, nand_35_out, nand_36_out);
  nand nand_80 (nand_80_out, nand_37_out, C);
  nand nand_81 (nand_81_out, D, E);
  nand nand_82 (nand_82_out, nand_38_out, B);
  nand nand_83 (nand_83_out, nand_39_out, nand_40_out);
  nand nand_84 (nand_84_out, nand_41_out, B);
  nand nand_85 (nand_85_out, C, D);
  nand nand_86 (nand_86_out, A, nand_42_out);
  nand nand_87 (nand_87_out, nand_43_out, E);
  nand nand_88 (nand_88_out, A, nand_44_out);
  nand nand_89 (nand_89_out, C, E);
  nand nand_90 (nand_90_out, A, nand_45_out);
  nand nand_91 (nand_91_out, C, D);
  nand nand_92 (nand_92_out, A, B);
  nand nand_93 (nand_93_out, nand_46_out, nand_47_out);
  nand nand_94 (nand_94_out, A, B);
  nand nand_95 (nand_95_out, nand_48_out, nand_49_out);
  nand nand_96 (nand_96_out, nand_50_out, nand_50_out);
  nand nand_97 (nand_97_out, nand_51_out, nand_51_out);
  nand nand_98 (nand_98_out, E, E);
  nand nand_99 (nand_99_out, nand_52_out, nand_52_out);
  nand nand_100 (nand_100_out, A, A);
  nand nand_101 (nand_101_out, nand_53_out, nand_53_out);
  nand nand_102 (nand_102_out, nand_54_out, nand_54_out);
  nand nand_103 (nand_103_out, nand_55_out, nand_55_out);
  nand nand_104 (nand_104_out, D, D);
  nand nand_105 (nand_105_out, C, C);
  nand nand_106 (nand_106_out, nand_56_out, nand_56_out);
  nand nand_107 (nand_107_out, nand_57_out, nand_57_out);
  nand nand_108 (nand_108_out, nand_58_out, nand_58_out);
  nand nand_109 (nand_109_out, A, A);
  nand nand_110 (nand_110_out, C, C);
  nand nand_111 (nand_111_out, D, D);
  nand nand_112 (nand_112_out, nand_59_out, nand_59_out);
  nand nand_113 (nand_113_out, nand_60_out, nand_60_out);
  nand nand_114 (nand_114_out, nand_61_out, nand_61_out);
  nand nand_115 (nand_115_out, C, C);
  nand nand_116 (nand_116_out, B, B);
  nand nand_117 (nand_117_out, nand_62_out, nand_62_out);
  nand nand_118 (nand_118_out, nand_63_out, nand_63_out);
  nand nand_119 (nand_119_out, nand_64_out, nand_64_out);
  nand nand_120 (nand_120_out, nand_65_out, nand_65_out);
  nand nand_121 (nand_121_out, C, C);
  nand nand_122 (nand_122_out, nand_66_out, nand_66_out);
  nand nand_123 (nand_123_out, D, D);
  nand nand_124 (nand_124_out, nand_67_out, nand_67_out);
  nand nand_125 (nand_125_out, E, E);
  nand nand_126 (nand_126_out, nand_68_out, nand_68_out);
  nand nand_127 (nand_127_out, D, D);
  nand nand_128 (nand_128_out, C, C);
  nand nand_129 (nand_129_out, nand_69_out, nand_69_out);
  nand nand_130 (nand_130_out, nand_70_out, nand_70_out);
  nand nand_131 (nand_131_out, nand_71_out, nand_71_out);
  nand nand_132 (nand_132_out, B, B);
  nand nand_133 (nand_133_out, D, D);
  nand nand_134 (nand_134_out, E, E);
  nand nand_135 (nand_135_out, nand_72_out, nand_72_out);
  nand nand_136 (nand_136_out, nand_73_out, nand_73_out);
  nand nand_137 (nand_137_out, nand_74_out, nand_74_out);
  nand nand_138 (nand_138_out, nand_75_out, nand_75_out);
  nand nand_139 (nand_139_out, C, C);
  nand nand_140 (nand_140_out, nand_76_out, nand_76_out);
  nand nand_141 (nand_141_out, nand_77_out, nand_77_out);
  nand nand_142 (nand_142_out, nand_78_out, nand_78_out);
  nand nand_143 (nand_143_out, nand_79_out, nand_79_out);
  nand nand_144 (nand_144_out, nand_80_out, nand_80_out);
  nand nand_145 (nand_145_out, nand_81_out, nand_81_out);
  nand nand_146 (nand_146_out, nand_82_out, nand_82_out);
  nand nand_147 (nand_147_out, nand_83_out, nand_83_out);
  nand nand_148 (nand_148_out, nand_84_out, nand_84_out);
  nand nand_149 (nand_149_out, nand_85_out, nand_85_out);
  nand nand_150 (nand_150_out, nand_86_out, nand_86_out);
  nand nand_151 (nand_151_out, nand_87_out, nand_87_out);
  nand nand_152 (nand_152_out, C, C);
  nand nand_153 (nand_153_out, E, E);
  nand nand_154 (nand_154_out, nand_88_out, nand_88_out);
  nand nand_155 (nand_155_out, nand_89_out, nand_89_out);
  nand nand_156 (nand_156_out, nand_90_out, nand_90_out);
  nand nand_157 (nand_157_out, nand_91_out, nand_91_out);
  nand nand_158 (nand_158_out, nand_92_out, nand_92_out);
  nand nand_159 (nand_159_out, nand_93_out, nand_93_out);
  nand nand_160 (nand_160_out, nand_94_out, nand_94_out);
  nand nand_161 (nand_161_out, nand_95_out, nand_95_out);
  nand nand_162 (nand_162_out, nand_96_out, E);
  nand nand_163 (nand_163_out, nand_97_out, nand_98_out);
  nand nand_164 (nand_164_out, nand_99_out, E);
  nand nand_165 (nand_165_out, nand_100_out, C);
  nand nand_166 (nand_166_out, nand_101_out, nand_102_out);
  nand nand_167 (nand_167_out, nand_103_out, nand_104_out);
  nand nand_168 (nand_168_out, A, nand_105_out);
  nand nand_169 (nand_169_out, nand_106_out, nand_107_out);
  nand nand_170 (nand_170_out, nand_108_out, D);
  nand nand_171 (nand_171_out, nand_109_out, B);
  nand nand_172 (nand_172_out, nand_110_out, nand_111_out);
  nand nand_173 (nand_173_out, nand_112_out, nand_113_out);
  nand nand_174 (nand_174_out, nand_114_out, nand_115_out);
  nand nand_175 (nand_175_out, A, nand_116_out);
  nand nand_176 (nand_176_out, nand_117_out, nand_118_out);
  nand nand_177 (nand_177_out, nand_119_out, C);
  nand nand_178 (nand_178_out, nand_120_out, nand_121_out);
  nand nand_179 (nand_179_out, nand_122_out, nand_123_out);
  nand nand_180 (nand_180_out, nand_124_out, nand_125_out);
  nand nand_181 (nand_181_out, nand_126_out, nand_127_out);
  nand nand_182 (nand_182_out, A, nand_128_out);
  nand nand_183 (nand_183_out, nand_129_out, E);
  nand nand_184 (nand_184_out, nand_130_out, nand_131_out);
  nand nand_185 (nand_185_out, nand_132_out, C);
  nand nand_186 (nand_186_out, nand_133_out, nand_134_out);
  nand nand_187 (nand_187_out, nand_135_out, nand_136_out);
  nand nand_188 (nand_188_out, nand_137_out, nand_138_out);
  nand nand_189 (nand_189_out, A, nand_139_out);
  nand nand_190 (nand_190_out, nand_140_out, nand_141_out);
  nand nand_191 (nand_191_out, nand_142_out, nand_143_out);
  nand nand_192 (nand_192_out, nand_144_out, nand_145_out);
  nand nand_193 (nand_193_out, nand_146_out, nand_147_out);
  nand nand_194 (nand_194_out, nand_148_out, nand_149_out);
  nand nand_195 (nand_195_out, nand_150_out, nand_151_out);
  nand nand_196 (nand_196_out, A, nand_152_out);
  nand nand_197 (nand_197_out, D, nand_153_out);
  nand nand_198 (nand_198_out, nand_154_out, nand_155_out);
  nand nand_199 (nand_199_out, nand_156_out, nand_157_out);
  nand nand_200 (nand_200_out, nand_158_out, nand_159_out);
  nand nand_201 (nand_201_out, nand_160_out, nand_161_out);
  nand nand_202 (nand_202_out, nand_162_out, nand_163_out);
  nand nand_203 (nand_203_out, nand_164_out, nand_165_out);
  nand nand_204 (nand_204_out, nand_166_out, nand_167_out);
  nand nand_205 (nand_205_out, nand_168_out, nand_168_out);
  nand nand_206 (nand_206_out, E, E);
  nand nand_207 (nand_207_out, nand_169_out, nand_170_out);
  nand nand_208 (nand_208_out, nand_171_out, nand_171_out);
  nand nand_209 (nand_209_out, nand_172_out, nand_172_out);
  nand nand_210 (nand_210_out, nand_173_out, nand_174_out);
  nand nand_211 (nand_211_out, nand_175_out, nand_175_out);
  nand nand_212 (nand_212_out, E, E);
  nand nand_213 (nand_213_out, nand_176_out, nand_177_out);
  nand nand_214 (nand_214_out, nand_178_out, nand_179_out);
  nand nand_215 (nand_215_out, nand_180_out, nand_181_out);
  nand nand_216 (nand_216_out, nand_182_out, nand_182_out);
  nand nand_217 (nand_217_out, E, E);
  nand nand_218 (nand_218_out, nand_183_out, nand_184_out);
  nand nand_219 (nand_219_out, nand_185_out, nand_185_out);
  nand nand_220 (nand_220_out, nand_186_out, nand_186_out);
  nand nand_221 (nand_221_out, nand_187_out, nand_188_out);
  nand nand_222 (nand_222_out, nand_189_out, nand_189_out);
  nand nand_223 (nand_223_out, D, D);
  nand nand_224 (nand_224_out, nand_190_out, nand_191_out);
  nand nand_225 (nand_225_out, nand_192_out, nand_193_out);
  nand nand_226 (nand_226_out, nand_194_out, nand_195_out);
  nand nand_227 (nand_227_out, nand_196_out, nand_196_out);
  nand nand_228 (nand_228_out, nand_197_out, nand_197_out);
  nand nand_229 (nand_229_out, nand_198_out, nand_199_out);
  nand nand_230 (nand_230_out, nand_200_out, nand_201_out);
  nand nand_231 (nand_231_out, nand_202_out, nand_202_out);
  nand nand_232 (nand_232_out, nand_203_out, nand_203_out);
  nand nand_233 (nand_233_out, nand_204_out, nand_204_out);
  nand nand_234 (nand_234_out, nand_205_out, nand_206_out);
  nand nand_235 (nand_235_out, nand_207_out, nand_207_out);
  nand nand_236 (nand_236_out, nand_208_out, nand_209_out);
  nand nand_237 (nand_237_out, nand_210_out, nand_210_out);
  nand nand_238 (nand_238_out, nand_211_out, nand_212_out);
  nand nand_239 (nand_239_out, nand_213_out, nand_213_out);
  nand nand_240 (nand_240_out, nand_214_out, nand_214_out);
  nand nand_241 (nand_241_out, nand_215_out, nand_215_out);
  nand nand_242 (nand_242_out, nand_216_out, nand_217_out);
  nand nand_243 (nand_243_out, nand_218_out, nand_218_out);
  nand nand_244 (nand_244_out, nand_219_out, nand_220_out);
  nand nand_245 (nand_245_out, nand_221_out, nand_221_out);
  nand nand_246 (nand_246_out, nand_222_out, nand_223_out);
  nand nand_247 (nand_247_out, nand_224_out, nand_224_out);
  nand nand_248 (nand_248_out, nand_225_out, nand_225_out);
  nand nand_249 (nand_249_out, nand_226_out, nand_226_out);
  nand nand_250 (nand_250_out, nand_227_out, nand_228_out);
  nand nand_251 (nand_251_out, nand_229_out, nand_229_out);
  nand nand_252 (nand_252_out, nand_230_out, nand_230_out);
  nand nand_253 (nand_253_out, nand_231_out, nand_232_out);
  nand nand_254 (nand_254_out, nand_233_out, nand_234_out);
  nand nand_255 (nand_255_out, nand_235_out, nand_236_out);
  nand nand_256 (nand_256_out, nand_237_out, nand_238_out);
  nand nand_257 (nand_257_out, nand_239_out, nand_240_out);
  nand nand_258 (nand_258_out, nand_241_out, nand_242_out);
  nand nand_259 (nand_259_out, nand_243_out, nand_244_out);
  nand nand_260 (nand_260_out, nand_245_out, nand_246_out);
  nand nand_261 (nand_261_out, nand_247_out, nand_248_out);
  nand nand_262 (nand_262_out, nand_249_out, nand_250_out);
  nand nand_263 (L5, nand_251_out, nand_252_out);
  nand nand_264 (nand_264_out, nand_253_out, nand_253_out);
  nand nand_265 (nand_265_out, nand_254_out, nand_254_out);
  nand nand_266 (nand_266_out, nand_255_out, nand_255_out);
  nand nand_267 (nand_267_out, nand_256_out, nand_256_out);
  nand nand_268 (nand_268_out, nand_257_out, nand_257_out);
  nand nand_269 (nand_269_out, nand_258_out, nand_258_out);
  nand nand_270 (nand_270_out, nand_259_out, nand_259_out);
  nand nand_271 (nand_271_out, nand_260_out, nand_260_out);
  nand nand_272 (nand_272_out, nand_261_out, nand_261_out);
  nand nand_273 (nand_273_out, nand_262_out, nand_262_out);
  nand nand_274 (L0, nand_264_out, nand_265_out);
  nand nand_275 (L1, nand_266_out, nand_267_out);
  nand nand_276 (L2, nand_268_out, nand_269_out);
  nand nand_277 (L3, nand_270_out, nand_271_out);
  nand nand_278 (L4, nand_272_out, nand_273_out);
endmodule

module Registrador (
  input  in_1,
  input  in_2,
  input  in_3,
  input  in_4,
  input  in_5,
  input  in_6,
  input  in_7,
  input  in_8,
  output out_9,
  output out_10,
  output out_11,
  output out_12,
  output out_13,
  output out_14
);

  D_Flip_Flop d_ff_1 (.clk(in_7), .D(in_1), .Q(out_9), .reset(in_8));  // open: Qn, preset, en
  D_Flip_Flop d_ff_2 (.clk(in_7), .D(in_2), .Q(out_10), .reset(in_8));  // open: Qn, preset, en
  D_Flip_Flop d_ff_3 (.clk(in_7), .D(in_3), .Q(out_11), .reset(in_8));  // open: Qn, preset, en
  D_Flip_Flop d_ff_4 (.clk(in_7), .D(in_4), .Q(out_12), .reset(in_8));  // open: Qn, preset, en
  D_Flip_Flop d_ff_5 (.clk(in_7), .D(in_5), .Q(out_13), .reset(in_8));  // open: Qn, preset, en
  D_Flip_Flop d_ff_6 (.clk(in_7), .D(in_6), .Q(out_14), .reset(in_8));  // open: Qn, preset, en
endmodule

module Uniao (
  input  in_1,
  input  in_2,
  input  in_3,
  input  in_4,
  input  in_5,
  input  in_6,
  input  in_7,
  output out_8,
  output out_9,
  output out_10,
  output out_11,
  output out_12,
  output out_13
);

  wire main_1_l0, main_1_l1, main_1_l2, main_1_l3, main_1_l4, main_1_l5;

  main main_1 (
    .A(in_1), .B(in_2), .C(in_3), .D(in_4), .E(in_5), .L0(main_1_l0), .L1(main_1_l1), .L2(main_1_l2),
    .L3(main_1_l3), .L4(main_1_l4), .L5(main_1_l5));
  Registrador registrador_1 (
    .in_1(main_1_l0), .in_2(main_1_l1), .in_3(main_1_l2), .in_4(main_1_l3), .in_5(main_1_l4),
    .in_6(main_1_l5), .in_7(in_6), .in_8(in_7), .out_9(out_8), .out_10(out_9), .out_11(out_10),
    .out_12(out_11), .out_13(out_12), .out_14(out_13));
endmodule

module Principal (
  input  in_1,
  input  Reset
);

  wire clock_1_out, decoder_1_out0, decoder_1_out1, decoder_1_out2, decoder_1_out3, decoder_1_out4,
       decoder_1_out5, decoder_1_out6, decoder_1_out7, main_1_l0, main_1_l1, main_1_l2, main_1_l3, main_1_l4,
       main_1_l5, main_2_l0, main_2_l1, main_2_l2, main_2_l3, main_2_l4, main_2_l5, main_3_l0, main_3_l1,
       main_3_l2, main_3_l3, main_3_l4, main_3_l5, main_4_l0, main_4_l1, main_4_l2, main_4_l3, main_4_l4,
       main_4_l5, main_5_l0, main_5_l1, main_5_l2, main_5_l3, main_5_l4, main_5_l5, main_6_l0, main_6_l1,
       main_6_l2, main_6_l3, main_6_l4, main_6_l5, main_7_l0, main_7_l1, main_7_l2, main_7_l3, main_7_l4,
       main_7_l5, main_8_l0, main_8_l1, main_8_l2, main_8_l3, main_8_l4, main_8_l5, registrador_1_out_9,
       registrador_1_out_10, registrador_1_out_11, registrador_1_out_12, registrador_1_out_13,
       registrador_1_out_14, registrador_2_out_9, registrador_2_out_10, registrador_2_out_11,
       registrador_2_out_12, registrador_2_out_13, registrador_2_out_14, registrador_3_out_9,
       registrador_3_out_10, registrador_3_out_11, registrador_3_out_12, registrador_3_out_13,
       registrador_3_out_14, registrador_4_out_9, registrador_4_out_10, registrador_4_out_11,
       registrador_4_out_12, registrador_4_out_13, registrador_4_out_14, registrador_5_out_9,
       registrador_5_out_10, registrador_5_out_11, registrador_5_out_12, registrador_5_out_13,
       registrador_5_out_14, registrador_6_out_9, registrador_6_out_10, registrador_6_out_11,
       registrador_6_out_12, registrador_6_out_13, registrador_6_out_14, registrador_7_out_9,
       registrador_7_out_10, registrador_7_out_11, registrador_7_out_12, registrador_7_out_13,
       registrador_7_out_14, registrador_8_out_9, registrador_8_out_10, registrador_8_out_11,
       registrador_8_out_12, registrador_8_out_13, registrador_8_out_14;
  wire [2:0] counter_2_q;
  wire [4:0] ram_1_data;
  wire [7:0] counter_1_q;

  Counter counter_1 (.Q(counter_1_q), .clk(clock_1_out), .clr(Reset));  // open: load, D, count, carry
  RAM #(.dataWidth(5)) ram_1 (.addr(counter_1_q), .data(ram_1_data), .clk(clock_1_out), .ld(in_1));  // open: sel, clr
  Clock clock_1 (.out(clock_1_out));
  Decoder #(.select(3)) decoder_1 (
    .out0(decoder_1_out0), .out1(decoder_1_out1), .out2(decoder_1_out2), .out3(decoder_1_out3),
    .out4(decoder_1_out4), .out5(decoder_1_out5), .out6(decoder_1_out6), .out7(decoder_1_out7),
    .sel(counter_2_q));  // open: en
  Counter #(.width(3), .max('h7)) counter_2 (.Q(counter_2_q), .clk(clock_1_out));  // open: load, D, count, carry, clr
  main main_1 (
    .A(ram_1_data[0]), .B(ram_1_data[1]), .C(ram_1_data[2]), .D(ram_1_data[3]), .E(ram_1_data[4]),
    .L0(main_1_l0), .L1(main_1_l1), .L2(main_1_l2), .L3(main_1_l3), .L4(main_1_l4), .L5(main_1_l5));
  main main_2 (
    .A(ram_1_data[0]), .B(ram_1_data[1]), .C(ram_1_data[2]), .D(ram_1_data[3]), .E(ram_1_data[4]),
    .L0(main_2_l0), .L1(main_2_l1), .L2(main_2_l2), .L3(main_2_l3), .L4(main_2_l4), .L5(main_2_l5));
  Registrador registrador_1 (
    .in_1(main_1_l0), .in_2(main_1_l1), .in_3(main_1_l2), .in_4(main_1_l3), .in_5(main_1_l4),
    .in_6(main_1_l5), .in_7(decoder_1_out0), .in_8(Reset), .out_9(registrador_1_out_9),
    .out_10(registrador_1_out_10), .out_11(registrador_1_out_11), .out_12(registrador_1_out_12),
    .out_13(registrador_1_out_13), .out_14(registrador_1_out_14));
  Registrador registrador_2 (
    .in_1(main_2_l0), .in_2(main_2_l1), .in_3(main_2_l2), .in_4(main_2_l3), .in_5(main_2_l4),
    .in_6(main_2_l5), .in_7(decoder_1_out4), .in_8(Reset), .out_9(registrador_2_out_9),
    .out_10(registrador_2_out_10), .out_11(registrador_2_out_11), .out_12(registrador_2_out_12),
    .out_13(registrador_2_out_13), .out_14(registrador_2_out_14));
  LED led_1 (.in(registrador_1_out_12));
  LED led_2 (.in(registrador_1_out_9));
  LED led_3 (.in(registrador_1_out_13));
  LED led_4 (.in(registrador_1_out_10));
  LED led_5 (.in(registrador_1_out_11));
  LED led_6 (.in(registrador_1_out_14));
  LED led_7 (.in(registrador_2_out_9));
  LED led_8 (.in(registrador_2_out_12));
  LED led_9 (.in(registrador_2_out_13));
  LED led_10 (.in(registrador_2_out_10));
  LED led_11 (.in(registrador_2_out_14));
  LED led_12 (.in(registrador_2_out_11));
  main main_3 (
    .A(ram_1_data[0]), .B(ram_1_data[1]), .C(ram_1_data[2]), .D(ram_1_data[3]), .E(ram_1_data[4]),
    .L0(main_3_l0), .L1(main_3_l1), .L2(main_3_l2), .L3(main_3_l3), .L4(main_3_l4), .L5(main_3_l5));
  main main_4 (
    .A(ram_1_data[0]), .B(ram_1_data[1]), .C(ram_1_data[2]), .D(ram_1_data[3]), .E(ram_1_data[4]),
    .L0(main_4_l0), .L1(main_4_l1), .L2(main_4_l2), .L3(main_4_l3), .L4(main_4_l4), .L5(main_4_l5));
  Registrador registrador_3 (
    .in_1(main_3_l0), .in_2(main_3_l1), .in_3(main_3_l2), .in_4(main_3_l3), .in_5(main_3_l4),
    .in_6(main_3_l5), .in_7(decoder_1_out5), .in_8(Reset), .out_9(registrador_3_out_9),
    .out_10(registrador_3_out_10), .out_11(registrador_3_out_11), .out_12(registrador_3_out_12),
    .out_13(registrador_3_out_13), .out_14(registrador_3_out_14));
  LED led_13 (.in(registrador_4_out_9));
  LED led_14 (.in(registrador_4_out_10));
  LED led_15 (.in(registrador_4_out_11));
  Registrador registrador_4 (
    .in_1(main_4_l0), .in_2(main_4_l1), .in_3(main_4_l2), .in_4(main_4_l3), .in_5(main_4_l4),
    .in_6(main_4_l5), .in_7(decoder_1_out1), .in_8(Reset), .out_9(registrador_4_out_9),
    .out_10(registrador_4_out_10), .out_11(registrador_4_out_11), .out_12(registrador_4_out_12),
    .out_13(registrador_4_out_13), .out_14(registrador_4_out_14));
  LED led_16 (.in(registrador_3_out_9));
  LED led_17 (.in(registrador_3_out_12));
  LED led_18 (.in(registrador_3_out_13));
  LED led_19 (.in(registrador_3_out_10));
  LED led_20 (.in(registrador_3_out_14));
  LED led_21 (.in(registrador_3_out_11));
  LED led_22 (.in(registrador_4_out_12));
  LED led_23 (.in(registrador_4_out_13));
  LED led_24 (.in(registrador_4_out_14));
  main main_5 (
    .A(ram_1_data[0]), .B(ram_1_data[1]), .C(ram_1_data[2]), .D(ram_1_data[3]), .E(ram_1_data[4]),
    .L0(main_5_l0), .L1(main_5_l1), .L2(main_5_l2), .L3(main_5_l3), .L4(main_5_l4), .L5(main_5_l5));
  main main_6 (
    .A(ram_1_data[0]), .B(ram_1_data[1]), .C(ram_1_data[2]), .D(ram_1_data[3]), .E(ram_1_data[4]),
    .L0(main_6_l0), .L1(main_6_l1), .L2(main_6_l2), .L3(main_6_l3), .L4(main_6_l4), .L5(main_6_l5));
  Registrador registrador_5 (
    .in_1(main_5_l0), .in_2(main_5_l1), .in_3(main_5_l2), .in_4(main_5_l3), .in_5(main_5_l4),
    .in_6(main_5_l5), .in_7(decoder_1_out6), .in_8(Reset), .out_9(registrador_5_out_9),
    .out_10(registrador_5_out_10), .out_11(registrador_5_out_11), .out_12(registrador_5_out_12),
    .out_13(registrador_5_out_13), .out_14(registrador_5_out_14));
  LED led_25 (.in(registrador_6_out_9));
  LED led_26 (.in(registrador_6_out_10));
  LED led_27 (.in(registrador_6_out_11));
  Registrador registrador_6 (
    .in_1(main_6_l0), .in_2(main_6_l1), .in_3(main_6_l2), .in_4(main_6_l3), .in_5(main_6_l4),
    .in_6(main_6_l5), .in_7(decoder_1_out2), .in_8(Reset), .out_9(registrador_6_out_9),
    .out_10(registrador_6_out_10), .out_11(registrador_6_out_11), .out_12(registrador_6_out_12),
    .out_13(registrador_6_out_13), .out_14(registrador_6_out_14));
  LED led_28 (.in(registrador_5_out_9));
  LED led_29 (.in(registrador_5_out_10));
  LED led_30 (.in(registrador_5_out_11));
  LED led_31 (.in(registrador_6_out_12));
  LED led_32 (.in(registrador_6_out_13));
  LED led_33 (.in(registrador_6_out_14));
  LED led_34 (.in(registrador_5_out_12));
  LED led_35 (.in(registrador_5_out_13));
  LED led_36 (.in(registrador_5_out_14));
  main main_7 (
    .A(ram_1_data[0]), .B(ram_1_data[1]), .C(ram_1_data[2]), .D(ram_1_data[3]), .E(ram_1_data[4]),
    .L0(main_7_l0), .L1(main_7_l1), .L2(main_7_l2), .L3(main_7_l3), .L4(main_7_l4), .L5(main_7_l5));
  main main_8 (
    .A(ram_1_data[0]), .B(ram_1_data[1]), .C(ram_1_data[2]), .D(ram_1_data[3]), .E(ram_1_data[4]),
    .L0(main_8_l0), .L1(main_8_l1), .L2(main_8_l2), .L3(main_8_l3), .L4(main_8_l4), .L5(main_8_l5));
  Registrador registrador_7 (
    .in_1(main_7_l0), .in_2(main_7_l1), .in_3(main_7_l2), .in_4(main_7_l3), .in_5(main_7_l4),
    .in_6(main_7_l5), .in_7(decoder_1_out3), .in_8(Reset), .out_9(registrador_7_out_9),
    .out_10(registrador_7_out_10), .out_11(registrador_7_out_11), .out_12(registrador_7_out_12),
    .out_13(registrador_7_out_13), .out_14(registrador_7_out_14));
  LED led_37 (.in(registrador_8_out_9));
  LED led_38 (.in(registrador_8_out_10));
  LED led_39 (.in(registrador_8_out_11));
  Registrador registrador_8 (
    .in_1(main_8_l0), .in_2(main_8_l1), .in_3(main_8_l2), .in_4(main_8_l3), .in_5(main_8_l4),
    .in_6(main_8_l5), .in_7(decoder_1_out7), .in_8(Reset), .out_9(registrador_8_out_9),
    .out_10(registrador_8_out_10), .out_11(registrador_8_out_11), .out_12(registrador_8_out_12),
    .out_13(registrador_8_out_13), .out_14(registrador_8_out_14));
  LED led_40 (.in(registrador_7_out_9));
  LED led_41 (.in(registrador_7_out_10));
  LED led_42 (.in(registrador_7_out_11));
  LED led_43 (.in(registrador_8_out_12));
  LED led_44 (.in(registrador_8_out_13));
  LED led_45 (.in(registrador_8_out_14));
  LED led_46 (.in(registrador_7_out_12));
  LED led_47 (.in(registrador_7_out_13));
  LED led_48 (.in(registrador_7_out_14));
endmodule
