// Logisim project entradaL5.circ as structural Verilog: 1 circuit, main circuit main
module main (
  input  A,
  input  B,
  input  C,
  input  D,
  input  E,
  output L5
);

  wire and_1_out, and_2_out, and_3_out, and_4_out, and_5_out, and_6_out, and_7_out, and_8_out, and_9_out,
       and_10_out, nand_1_out, nand_2_out, nand_3_out, nand_4_out, nand_5_out, nand_6_out, nand_7_out,
       nand_8_out, nand_9_out, nand_10_out;

  nand nand_1 (nand_1_out, B, B);
  nand nand_2 (nand_2_out, B, B);
  nand nand_3 (nand_3_out, C, C);
  nand nand_4 (nand_4_out, D, D);
  nand nand_5 (nand_5_out, C, C);
  nand nand_6 (nand_6_out, E, E);
  and and_1 (and_1_out, A, nand_1_out);
  and and_2 (and_2_out, C, E);
  and and_3 (and_3_out, A, nand_2_out);
  and and_4 (and_4_out, C, D);
  and and_5 (and_5_out, A, B);
  and and_6 (and_6_out, nand_3_out, nand_4_out);
  and and_7 (and_7_out, A, B);
  and and_8 (and_8_out, nand_5_out, nand_6_out);
  nand nand_7 (nand_7_out, and_1_out, and_2_out);
  nand nand_8 (nand_8_out, and_3_out, and_4_out);
  nand nand_9 (nand_9_out, and_5_out, and_6_out);
  nand nand_10 (nand_10_out, and_7_out, and_8_out);
  and and_9 (and_9_out, nand_7_out, nand_8_out);
  and and_10 (and_10_out, nand_9_out, nand_10_out);
  nand nand_11 (L5, and_9_out, and_10_out);
endmodule
